// Digital circuit adder.dig as structural Verilog
module adder (
  input  i_1,
  input  i_2,
  input  i_3,
  input  i_4,
  input  c_in,
  output o,
  output out_7
);

  // Or or_1 is placed but not wired

  // Notes on the sheet:
  //   c_in: 1 when we add 1 from previous operation
  //   o: 1 when there is overflow / undeflow
endmodule
