// Digital circuit cpu.dig as structural Verilog
module cpu (
  input  in_1,
  input  in_2,
  input  in_3,
  input  clk
);

  wire adder_1_p10, adder_1_p11, adder_2_p10, adder_2_p11, adder_2_p12, adder_2_p13, alu_out, and_1_out,
       and_2_out, and_3_out, and_4_out, and_5_out, and_6_out, button_1_out, button_2_out,
       counter_resetable_1_o_0, counter_resetable_1_o_1, counter_resetable_1_o_2, counter_resetable_1_o_3,
       counter_resetable_2_o_0, counter_resetable_2_o_1, counter_resetable_2_o_2, counter_resetable_2_o_3,
       decoder_6_to_64_1_p3, decoder_6_to_64_1_p4, decoder_6_to_64_1_p5, decoder_6_to_64_1_p6,
       decoder_6_to_64_1_p8, decoder_6_to_64_1_p9, decoder_6_to_64_1_p10, decoder_6_to_64_1_p11,
       decoder_6_to_64_1_p12, decoder_6_to_64_1_p13, decoder_6_to_64_1_p14, decoder_6_to_64_1_p15,
       decoder_6_to_64_1_p16, decoder_6_to_64_1_p17, decoder_6_to_64_1_p18, decoder_6_to_64_1_p19,
       decoder_6_to_64_1_p20, decoder_6_to_64_1_p21, decoder_6_to_64_1_p22, decoder_6_to_64_1_p23,
       decoder_6_to_64_1_p24, decoder_6_to_64_1_p25, decoder_6_to_64_1_p26, decoder_6_to_64_1_p27,
       delay_1_out, madr_q_0, madr_q_1, madr_q_2, madr_q_3, memory2_1_o_0, memory2_1_o_1, memory2_1_o_2,
       memory2_1_o_3, memory2_1_o_4, memory2_1_o_5, memory2_1_o_6, memory2_1_o_7, nor_1_out, not_1_out,
       not_2_out, not_3_out, not_4_out, not_5_out, not_6_out, not_7_out, or_1_out, pc_reset, reg_A_zero,
       register_simple_1_q_0, register_simple_1_q_1, register_simple_1_q_2, register_simple_1_q_3,
       register_simple_2_q_0, register_simple_2_q_1, register_simple_2_q_2, register_simple_2_q_3,
       tri_state_buffer_4bit_1_o_0, tri_state_buffer_4bit_1_o_1, tri_state_buffer_4bit_1_o_2,
       tri_state_buffer_4bit_1_o_3, tri_state_buffer_4bit_2_o_0, tri_state_buffer_4bit_2_o_1,
       tri_state_buffer_4bit_2_o_2, tri_state_buffer_4bit_2_o_3, undriven, undriven_2, undriven_3;
  wire [15:0] control_bus;

  Delay #(.delayTime(20), .generic("this.Duration = args.duration;")) delay_1 (.in(button_1_out), .out(delay_1_out));
  Button #(.activeLow("true")) button_1 (.out(button_1_out));
  Button button_2 (.out(button_2_out));
  not not_1 (not_1_out, delay_1_out);
  or or_1 (or_1_out, control_bus[4], clk);
  and and_1 (and_1_out, button_1_out, not_1_out);
  or or_2 (pc_reset, and_1_out, in_3, button_2_out);
  not not_2 (not_2_out, pc_reset);
  not not_3 (not_3_out, or_1_out);
  and and_2 (and_2_out, not_2_out, not_3_out);
  counter_resetable counter_resetable_1 (
    .C(or_1_out), .R(and_5_out), .S(1'b0), .D_0(1'b0), .D_1(1'b0), .D_2(1'b0), .D_3(1'b0), .R_a(pc_reset),
    .O_0(counter_resetable_1_o_0), .O_1(counter_resetable_1_o_1), .O_2(counter_resetable_1_o_2),
    .O_3(counter_resetable_1_o_3));
  not not_4 (not_4_out, counter_resetable_1_o_0);
  not not_5 (not_5_out, counter_resetable_1_o_1);
  not not_6 (not_6_out, counter_resetable_1_o_2);
  not not_7 (not_7_out, counter_resetable_1_o_3);
  and and_3 (and_3_out, not_4_out, not_5_out, not_6_out, not_7_out);
  and and_4 (and_4_out, counter_resetable_1_o_0, not_5_out, not_6_out, not_7_out);
  and and_5 (and_5_out, counter_resetable_1_o_0, counter_resetable_1_o_2);
  // adder adder_1: pin names not known; wires that end beside it: 1'b0, 1'b0, 1'b1, 1'b0, 1'b0, counter_resetable_1_o_0, counter_resetable_1_o_1, counter_resetable_1_o_2, counter_resetable_1_o_3, adder_1_p10, adder_1_p11
  assign control_bus[0] = and_3_out ? and_3_out : 1'bz;  // Driver driver_1
  assign control_bus[1] = and_3_out ? and_3_out : 1'bz;  // Driver driver_2
  assign control_bus[3] = and_4_out ? and_4_out : 1'bz;  // Driver driver_3
  assign control_bus[6] = and_4_out ? and_4_out : 1'bz;  // Driver driver_4
  assign control_bus[2] = and_4_out ? and_4_out : 1'bz;  // Driver driver_5
  PullDown pulldown_1 (.out(control_bus[10]));
  PullDown pulldown_2 (.out(control_bus[11]));
  PullDown pulldown_3 (.out(control_bus[6]));
  PullDown pulldown_4 (.out(alu_out));
  PullDown pulldown_5 (.out(control_bus[8]));
  PullDown pulldown_6 (.out(control_bus[9]));
  PullDown pulldown_7 (.out(control_bus[2]));
  PullDown pulldown_8 (.out(control_bus[3]));
  PullDown pulldown_9 (.out(control_bus[4]));
  PullDown pulldown_10 (.out(control_bus[5]));
  nor nor_1 (nor_1_out, and_3_out, and_4_out);
  PullDown pulldown_11 (.out(control_bus[0]));
  PullDown pulldown_12 (.out(control_bus[1]));
  // decoder_6_to_64 decoder_6_to_64_1: pin names not known; wires that end beside it: adder_1_p10, adder_1_p11, decoder_6_to_64_1_p3, decoder_6_to_64_1_p4, decoder_6_to_64_1_p5, decoder_6_to_64_1_p6, nor_1_out, decoder_6_to_64_1_p8, decoder_6_to_64_1_p9, decoder_6_to_64_1_p10, decoder_6_to_64_1_p11, decoder_6_to_64_1_p12, decoder_6_to_64_1_p13, decoder_6_to_64_1_p14, decoder_6_to_64_1_p15, decoder_6_to_64_1_p16, decoder_6_to_64_1_p17, decoder_6_to_64_1_p18, decoder_6_to_64_1_p19, decoder_6_to_64_1_p20, decoder_6_to_64_1_p21, decoder_6_to_64_1_p22, decoder_6_to_64_1_p23, decoder_6_to_64_1_p24, decoder_6_to_64_1_p25, decoder_6_to_64_1_p26, decoder_6_to_64_1_p27, decoder_6_to_64_1_p12, decoder_6_to_64_1_p13, decoder_6_to_64_1_p14, decoder_6_to_64_1_p16, decoder_6_to_64_1_p17, decoder_6_to_64_1_p18, decoder_6_to_64_1_p21, decoder_6_to_64_1_p22, decoder_6_to_64_1_p25
  assign {control_bus[15:8], alu_out, control_bus[6:0]} = decoder_6_to_64_1_p20 ? 16'h204 : 16'bz;  // Driver driver_6
  assign {control_bus[15:8], alu_out, control_bus[6:0]} = decoder_6_to_64_1_p24 ? 16'hc00 : 16'bz;  // Driver driver_7
  assign {control_bus[15:8], alu_out, control_bus[6:0]} = decoder_6_to_64_1_p11 ? 16'h10 : 16'bz;  // Driver driver_8
  assign {control_bus[15:8], alu_out, control_bus[6:0]} = decoder_6_to_64_1_p15 ? 16'h24 : 16'bz;  // Driver driver_9
  assign {control_bus[15:8], alu_out, control_bus[6:0]} = decoder_6_to_64_1_p19 ? 16'h6 : 16'bz;  // Driver driver_10
  assign {control_bus[15:8], alu_out, control_bus[6:0]} = decoder_6_to_64_1_p23 ? 16'h6 : 16'bz;  // Driver driver_11
  assign {control_bus[15:8], alu_out, control_bus[6:0]} = undriven ? 16'ha0 : 16'bz;  // Driver driver_12
  assign {control_bus[15:8], alu_out, control_bus[6:0]} = undriven_2 ? 16'h144 : 16'bz;  // Driver driver_13
  assign {control_bus[15:8], alu_out, control_bus[6:0]} = undriven_3 ? {{7{1'b0}}, reg_A_zero, 1'b0, reg_A_zero, 6'b000100} : 16'bz;  // Driver driver_14
  register_simple madr (
    .E_out(control_bus[1]), .CLK(and_2_out), .D_0(tri_state_buffer_4bit_1_o_0),
    .D_1(tri_state_buffer_4bit_1_o_1), .D_2(tri_state_buffer_4bit_1_o_2), .D_3(tri_state_buffer_4bit_1_o_3),
    .Q_0(madr_q_0), .Q_1(madr_q_1), .Q_2(madr_q_2), .Q_3(madr_q_3));
  memory2 memory2_1 (
    .a_0(madr_q_0), .a_1(madr_q_1), .a_2(madr_q_2), .a_3(madr_q_3), .E(control_bus[10]), .C(and_2_out),
    .D_0(tri_state_buffer_4bit_1_o_0), .D_1(tri_state_buffer_4bit_1_o_1), .D_2(tri_state_buffer_4bit_1_o_2),
    .D_3(tri_state_buffer_4bit_1_o_3), .O_0(memory2_1_o_0), .O_1(memory2_1_o_1), .O_2(memory2_1_o_2),
    .O_3(memory2_1_o_3), .O_4(memory2_1_o_4), .O_5(memory2_1_o_5), .O_6(memory2_1_o_6), .O_7(memory2_1_o_7));
  tri_state_buffer_4bit tri_state_buffer_4bit_1 (
    .D_0(memory2_1_o_0), .D_1(memory2_1_o_1), .D_2(memory2_1_o_2), .D_3(memory2_1_o_3), .E(control_bus[2]),
    .O_0(tri_state_buffer_4bit_1_o_0), .O_1(tri_state_buffer_4bit_1_o_1), .O_2(tri_state_buffer_4bit_1_o_2),
    .O_3(tri_state_buffer_4bit_1_o_3));
  tri_state_buffer_4bit tri_state_buffer_4bit_2 (
    .D_0(memory2_1_o_4), .D_1(memory2_1_o_5), .D_2(memory2_1_o_6), .D_3(memory2_1_o_7), .E(control_bus[2]),
    .O_0(tri_state_buffer_4bit_2_o_0), .O_1(tri_state_buffer_4bit_2_o_1), .O_2(tri_state_buffer_4bit_2_o_2),
    .O_3(tri_state_buffer_4bit_2_o_3));
  register_simple Current_Instruction_HI (
    .E_out(control_bus[3]), .CLK(and_2_out), .D_0(tri_state_buffer_4bit_2_o_0),
    .D_1(tri_state_buffer_4bit_2_o_1), .D_2(tri_state_buffer_4bit_2_o_2), .D_3(tri_state_buffer_4bit_2_o_3),
    .Q_0(decoder_6_to_64_1_p3), .Q_1(decoder_6_to_64_1_p4), .Q_2(decoder_6_to_64_1_p5),
    .Q_3(decoder_6_to_64_1_p6));
  register_simple Current_Instruction_LO (
    .E_out(control_bus[3]), .CLK(and_2_out), .D_0(tri_state_buffer_4bit_1_o_0),
    .D_1(tri_state_buffer_4bit_1_o_1), .D_2(tri_state_buffer_4bit_1_o_2), .D_3(tri_state_buffer_4bit_1_o_3),
    .Q_0(decoder_6_to_64_1_p27), .Q_1(decoder_6_to_64_1_p10), .Q_2(decoder_6_to_64_1_p9),
    .Q_3(decoder_6_to_64_1_p8));
  and and_6 (and_6_out, control_bus[6], and_2_out);
  counter_resetable counter_resetable_2 (
    .C(and_6_out), .R(1'b0), .S(control_bus[8]), .D_0(tri_state_buffer_4bit_1_o_0),
    .D_1(tri_state_buffer_4bit_1_o_1), .D_2(tri_state_buffer_4bit_1_o_2), .D_3(tri_state_buffer_4bit_1_o_3),
    .R_a(pc_reset), .O_0(counter_resetable_2_o_0), .O_1(counter_resetable_2_o_1),
    .O_2(counter_resetable_2_o_2), .O_3(counter_resetable_2_o_3));
  tri_state_buffer_4bit tri_state_buffer_4bit_3 (
    .D_0(counter_resetable_2_o_0), .D_1(counter_resetable_2_o_1), .D_2(counter_resetable_2_o_2),
    .D_3(counter_resetable_2_o_3), .E(control_bus[0]), .O_0(tri_state_buffer_4bit_1_o_0),
    .O_1(tri_state_buffer_4bit_1_o_1), .O_2(tri_state_buffer_4bit_1_o_2), .O_3(tri_state_buffer_4bit_1_o_3));
  register_simple register_simple_1 (
    .E_out(control_bus[5]), .CLK(and_2_out), .D_0(tri_state_buffer_4bit_1_o_0),
    .D_1(tri_state_buffer_4bit_1_o_1), .D_2(tri_state_buffer_4bit_1_o_2), .D_3(tri_state_buffer_4bit_1_o_3),
    .Q_0(register_simple_1_q_0), .Q_1(register_simple_1_q_1), .Q_2(register_simple_1_q_2),
    .Q_3(register_simple_1_q_3));
  register_simple register_simple_2 (
    .E_out(control_bus[9]), .CLK(and_2_out), .D_0(tri_state_buffer_4bit_1_o_0),
    .D_1(tri_state_buffer_4bit_1_o_1), .D_2(tri_state_buffer_4bit_1_o_2), .D_3(tri_state_buffer_4bit_1_o_3),
    .Q_0(register_simple_2_q_0), .Q_1(register_simple_2_q_1), .Q_2(register_simple_2_q_2),
    .Q_3(register_simple_2_q_3));
  tri_state_buffer_4bit tri_state_buffer_4bit_4 (
    .D_0(adder_2_p10), .D_1(adder_2_p11), .D_2(adder_2_p12), .D_3(adder_2_p13), .E(alu_out),
    .O_0(tri_state_buffer_4bit_1_o_0), .O_1(tri_state_buffer_4bit_1_o_1), .O_2(tri_state_buffer_4bit_1_o_2),
    .O_3(tri_state_buffer_4bit_1_o_3));
  tri_state_buffer_4bit tri_state_buffer_4bit_5 (
    .D_0(register_simple_1_q_0), .D_1(register_simple_1_q_1), .D_2(register_simple_1_q_2),
    .D_3(register_simple_1_q_3), .E(control_bus[11]), .O_0(tri_state_buffer_4bit_1_o_0),
    .O_1(tri_state_buffer_4bit_1_o_1), .O_2(tri_state_buffer_4bit_1_o_2), .O_3(tri_state_buffer_4bit_1_o_3));
  tri_state_buffer_4bit tri_state_buffer_4bit_6 (
    .D_0(register_simple_2_q_0), .D_1(register_simple_2_q_1), .D_2(register_simple_2_q_2),
    .D_3(register_simple_2_q_3), .E(in_1), .O_0(tri_state_buffer_4bit_1_o_0),
    .O_1(tri_state_buffer_4bit_1_o_1), .O_2(tri_state_buffer_4bit_1_o_2), .O_3(tri_state_buffer_4bit_1_o_3));
  nor nor_2 (reg_A_zero, register_simple_1_q_3, register_simple_1_q_2, register_simple_1_q_1, register_simple_1_q_0);
  // adder adder_2: pin names not known; wires that end beside it: in_2, register_simple_1_q_0, register_simple_1_q_1, register_simple_1_q_2, register_simple_1_q_3, register_simple_2_q_0, register_simple_2_q_1, register_simple_2_q_2, register_simple_2_q_3, adder_2_p10, adder_2_p11, adder_2_p12, adder_2_p13

  // Other names for the same wires on the sheet: pc_out = control_bus[0]; madr_in = control_bus[1];
  //   mem_out = control_bus[2]; curr_instr_in = control_bus[3]; halt = control_bus[4]; reg_A_in = control_bus[5];
  //   pc_inc = control_bus[6]; control_bus[7] = alu_out; pc_in = control_bus[8]; reg_B_in = control_bus[9];
  //   mem_in = control_bus[10]; reg_A_out = control_bus[11]

  // Notes on the sheet:
  //   clk: Hz: 100
  //   fibonnacci (big n):
  //   set adr of smaller ($00) <- 0;   mov 0, $1113  |  loadA 0; loadB $smaller; store
  //   set adr of bigger ($01) <- 1;    mov 1, $1114  | loadA 1; loadB $bigger; store
  //   set adr of n ($10) <- n;            mov 7, $1115  | 
  //   until n > 0 do ; .label-loop $3
  //   .  tmp <- bigger (mov $bigger, A; mov A, $tmp) (#2)   |  loadA bigger;loadB $tmp; store 
  //   .  bigger <- smaller+bigger (mov $smaller, B; save ALU to $bigger) (#2) |  sum (to adr?); store
  //   .  smaller <- tmp              (#1
  //   .  n--      (n - 1; jne);       mov $1115, regA; dec A???/ mov -1, regB; mov ALU, $1115  (3-4inst)
  //                                        jne label-loop ($3)
  //   return bigger;                hlt
  //   A <- 1  (store A adr)
  //   B <- 0
  //   $n <- n
  //   tmp <- B
  //   A <- A + B (store sum adr)
  //   B <- tmp
  //   dec $n
  //   jz
  //   hlt
  //   1110 jz imm: jump if regA==0 to imm
  //   mem-out; (pc-in and regA-zero) , (pc-inc and (clock))
  //   1100 jmp imm: 
  //   pc-in; mem-out, pc-inc (clock)
  //   0001 load imm to A
  //   .   mem-out, A-in
  //   0010 load mem[imm] to B
  //   .   mem-out, madr-in
  //   .   mem-out, regB-in
  //   0110 store regA to mem[imm]
  //       mem-out, madr-in
  //   .   reg-A-out, mem-in
  //   increase A by B (1010)
  //   regA-in, alu-out
  //   instruction set:
  //   0000 - halt
  //   0001 - load immediate reg-A
  //   0010 - load mem[imm] reg-B
  //   1010 (10 / 40) - alu to reg-A (add only?)
  //   1100 (12 / 48)- jmp imm
  //   1110 (14 / 56) - jz imm (jump to imm if reg-A == 0)
  //   **************************
  //   1111 (15 / 60)- jmp if
  //         load mem[imm] reg-A
  //         load mem[A] reg-A / or regB?
  //         store mem[immediate] reg-A
  //         store reg-A mem[reg-B] / or regB?
  //         mov A -> B / B -> A? (can we read operands from 2nd word?)
  //   jmp imm
  //   jmp reg-A
  //   jmp if(reg-A == 0)  to reg-B
  //   increase A by B
  //   negate A? B?
  //   *******************
  //   0010 - load immediate reg-B
  //   0011 - store reg-A mem[reg-B]
  //   .     reg-b out, madr-in
  //   .     reg-a out, mem-in
  //   0100 - jmp reg-A
  //   0101 - jmp reg-A if ???
  //   0110 - subtract reg-A - reg-B, save to reg-A (shrink A by B)
  //   0111 - output and stop
  //   .   reg-A out, halt
  //   1000 - loadA mem[A]
  //   1001 - loadB mem[A]
  //   --------------------------
endmodule
