// Digital circuit memory2.dig as structural Verilog
module memory2 (
  input  a_0,
  input  a_1,
  input  a_2,
  input  a_3,
  input  E,
  input  C,
  input  D_0,
  input  D_1,
  input  D_2,
  input  D_3,
  output O_0,
  output O_1,
  output O_2,
  output O_3,
  output O_4,
  output O_5,
  output O_6,
  output O_7
);

  wire and_1_out, and_2_out, and_3_out, and_4_out, and_5_out, and_6_out, and_7_out, and_8_out, and_9_out,
       and_10_out, and_11_out, and_12_out, and_13_out, and_14_out, and_15_out, and_16_out, not_1_out,
       not_2_out, not_3_out, not_4_out;
  wire [7:0] dipswitch_4_out;

  not not_1 (not_1_out, a_3);
  not not_2 (not_2_out, a_2);
  not not_3 (not_3_out, a_1);
  not not_4 (not_4_out, a_0);
  and and_1 (and_1_out, not_4_out, not_3_out, not_2_out, not_1_out);
  and and_2 (and_2_out, a_0, not_3_out, not_2_out, not_1_out);
  and and_3 (and_3_out, not_4_out, a_1, not_2_out, not_1_out);
  and and_4 (and_4_out, a_0, a_1, not_2_out, not_1_out);
  and and_5 (and_5_out, not_4_out, not_3_out, a_2, not_1_out);
  and and_6 (and_6_out, a_0, not_3_out, a_2, not_1_out);
  and and_7 (and_7_out, not_4_out, a_1, a_2, not_1_out);
  and and_8 (and_8_out, a_0, a_1, a_2, not_1_out);
  and and_9 (and_9_out, not_4_out, not_3_out, not_2_out, a_3);
  and and_10 (and_10_out, a_0, not_3_out, not_2_out, a_3);
  and and_11 (and_11_out, not_4_out, a_1, not_2_out, a_3);
  and and_12 (and_12_out, a_0, a_1, not_2_out, a_3);
  and and_13 (and_13_out, not_4_out, not_3_out, a_2, a_3);
  and and_14 (and_14_out, a_0, not_3_out, a_2, a_3);
  and and_15 (and_15_out, not_4_out, a_1, a_2, a_3);
  and and_16 (and_16_out, a_0, a_1, a_2, a_3);
  buffered_8bit_register buffered_8bit_register_1 (
    .CLK(C), .E_store(E), .E_ouput(and_3_out), .D_0(D_0), .D_1(D_1), .D_2(D_2), .D_3(D_3), .O_0(O_0),
    .O_1(O_1), .O_2(O_2), .O_3(O_3), .O_4(O_4), .O_5(O_5), .O_6(O_6), .O_7(O_7));
  buffered_8bit_register buffered_8bit_register_2 (
    .CLK(C), .E_store(E), .E_ouput(and_4_out), .D_0(D_0), .D_1(D_1), .D_2(D_2), .D_3(D_3), .O_0(O_0),
    .O_1(O_1), .O_2(O_2), .O_3(O_3), .O_4(O_4), .O_5(O_5), .O_6(O_6), .O_7(O_7));
  buffered_8bit_register buffered_8bit_register_3 (
    .CLK(C), .E_store(E), .E_ouput(and_5_out), .D_0(D_0), .D_1(D_1), .D_2(D_2), .D_3(D_3), .O_0(O_0),
    .O_1(O_1), .O_2(O_2), .O_3(O_3), .O_4(O_4), .O_5(O_5), .O_6(O_6), .O_7(O_7));
  buffered_8bit_register buffered_8bit_register_4 (
    .CLK(C), .E_store(E), .E_ouput(and_6_out), .D_0(D_0), .D_1(D_1), .D_2(D_2), .D_3(D_3), .O_0(O_0),
    .O_1(O_1), .O_2(O_2), .O_3(O_3), .O_4(O_4), .O_5(O_5), .O_6(O_6), .O_7(O_7));
  buffered_8bit_register buffered_8bit_register_5 (
    .CLK(C), .E_store(E), .E_ouput(and_7_out), .D_0(D_0), .D_1(D_1), .D_2(D_2), .D_3(D_3), .O_0(O_0),
    .O_1(O_1), .O_2(O_2), .O_3(O_3), .O_4(O_4), .O_5(O_5), .O_6(O_6), .O_7(O_7));
  buffered_8bit_register buffered_8bit_register_6 (
    .CLK(C), .E_store(E), .E_ouput(and_8_out), .D_0(D_0), .D_1(D_1), .D_2(D_2), .D_3(D_3), .O_0(O_0),
    .O_1(O_1), .O_2(O_2), .O_3(O_3), .O_4(O_4), .O_5(O_5), .O_6(O_6), .O_7(O_7));
  buffered_8bit_register buffered_8bit_register_7 (
    .CLK(C), .E_store(E), .E_ouput(and_9_out), .D_0(D_0), .D_1(D_1), .D_2(D_2), .D_3(D_3), .O_0(O_0),
    .O_1(O_1), .O_2(O_2), .O_3(O_3), .O_4(O_4), .O_5(O_5), .O_6(O_6), .O_7(O_7));
  buffered_8bit_register buffered_8bit_register_8 (
    .CLK(C), .E_store(E), .E_ouput(and_10_out), .D_0(D_0), .D_1(D_1), .D_2(D_2), .D_3(D_3), .O_0(O_0),
    .O_1(O_1), .O_2(O_2), .O_3(O_3), .O_4(O_4), .O_5(O_5), .O_6(O_6), .O_7(O_7));
  buffered_8bit_register buffered_8bit_register_9 (
    .CLK(C), .E_store(E), .E_ouput(and_11_out), .D_0(D_0), .D_1(D_1), .D_2(D_2), .D_3(D_3), .O_0(O_0),
    .O_1(O_1), .O_2(O_2), .O_3(O_3), .O_4(O_4), .O_5(O_5), .O_6(O_6), .O_7(O_7));
  buffered_8bit_register buffered_8bit_register_10 (
    .CLK(C), .E_store(E), .E_ouput(and_12_out), .D_0(D_0), .D_1(D_1), .D_2(D_2), .D_3(D_3), .O_0(O_0),
    .O_1(O_1), .O_2(O_2), .O_3(O_3), .O_4(O_4), .O_5(O_5), .O_6(O_6), .O_7(O_7));
  buffered_8bit_register buffered_8bit_register_11 (
    .CLK(C), .E_store(E), .E_ouput(and_13_out), .D_0(D_0), .D_1(D_1), .D_2(D_2), .D_3(D_3), .O_0(O_0),
    .O_1(O_1), .O_2(O_2), .O_3(O_3), .O_4(O_4), .O_5(O_5), .O_6(O_6), .O_7(O_7));
  buffered_8bit_register buffered_8bit_register_12 (
    .CLK(C), .E_store(E), .E_ouput(and_14_out), .D_0(D_0), .D_1(D_1), .D_2(D_2), .D_3(D_3), .O_0(O_0),
    .O_1(O_1), .O_2(O_2), .O_3(O_3), .O_4(O_4), .O_5(O_5), .O_6(O_6), .O_7(O_7));
  buffered_8bit_register buffered_8bit_register_13 (
    .CLK(C), .E_store(E), .E_ouput(and_15_out), .D_0(D_0), .D_1(D_1), .D_2(D_2), .D_3(D_3), .O_0(O_0),
    .O_1(O_1), .O_2(O_2), .O_3(O_3), .O_4(O_4), .O_5(O_5), .O_6(O_6), .O_7(O_7));
  buffered_8bit_register buffered_8bit_register_14 (
    .CLK(C), .E_store(E), .E_ouput(and_16_out), .D_0(D_0), .D_1(D_1), .D_2(D_2), .D_3(D_3), .O_0(O_0),
    .O_1(O_1), .O_2(O_2), .O_3(O_3), .O_4(O_4), .O_5(O_5), .O_6(O_6), .O_7(O_7));
  DipSwitch dipswitch_1 (.out(dipswitch_4_out[3]));
  DipSwitch dipswitch_2 (.out(dipswitch_4_out[2]));
  DipSwitch dipswitch_3 (.out(dipswitch_4_out[1]));
  DipSwitch dipswitch_4 (.out(dipswitch_4_out[0]));
  DipSwitch dipswitch_5 (.out(dipswitch_4_out[7]));
  DipSwitch dipswitch_6 (.out(dipswitch_4_out[6]));
  DipSwitch dipswitch_7 (.out(dipswitch_4_out[5]));
  DipSwitch dipswitch_8 (.out(dipswitch_4_out[4]));
  rom_buffer rom_buffer_1 (
    .E(and_1_out), .D(8'h16), .O_0(O_0), .O_1(O_1), .O_2(O_2), .O_3(O_3), .O_4(O_4), .O_5(O_5), .O_6(O_6),
    .O_7(O_7));
  rom_buffer rom_buffer_2 (
    .E(and_2_out), .D(dipswitch_4_out), .O_0(O_0), .O_1(O_1), .O_2(O_2), .O_3(O_3), .O_4(O_4), .O_5(O_5),
    .O_6(O_6), .O_7(O_7));

  // Notes on the sheet:
  //   0
  //   4
  //   8
  //   12
  //   15
endmodule

/* Test case:
C E   a_0 a_1 a_2 a_3   D_0 D_1 D_2 D_3   O_0 O_1 O_2 O_3

loop(v, 16)
 # save
 repeat(16)     C 1 bits(4, n)    bits(4, v)        bits(4, v)
 # read ignoring data
 repeat(16)     0 0 bits(4, n)    x x x x        bits(4, v)
 repeat(16)     0 1 bits(4, n)    bits(4, ~v)    bits(4, v)
 repeat(16)     C 0 bits(4, n)    bits(4, ~v)    bits(4, v)
end loop
*/
