// Digital circuit notepad.dig as structural Verilog
module notepad (
  input  S,
  input  R,
  input  clk,
  input  D,
  input  CLK_2,
  output Q,
  output Q_2,
  output Q_3,
  output Q_4
);

  wire and_1_out, and_2_out, and_3_out, and_4_out, d_flip_flop_1_q, nor_1_out, nor_2_out, not_1_out,
       not_2_out, not_3_out, not_4_out;

  not not_1 (not_1_out, clk);
  not not_2 (not_2_out, CLK_2);
  and and_1 (and_1_out, S, Q_4, not_1_out);
  and and_2 (and_2_out, not_1_out, Q_3, R);
  D_flip_flop d_flip_flop_1 (.D(D), .CLK(not_2_out), .Q(d_flip_flop_1_q));  // open: Q_2
  not not_3 (not_3_out, not_2_out);
  nor nor_1 (nor_1_out, and_1_out, nor_2_out);
  nor nor_2 (nor_2_out, nor_1_out, and_2_out);
  D_flip_flop d_flip_flop_2 (.D(d_flip_flop_1_q), .CLK(not_3_out), .Q(Q), .Q_2(Q_2));
  not not_4 (not_4_out, not_1_out);
  and and_3 (and_3_out, nor_2_out, not_4_out);
  and and_4 (and_4_out, not_4_out, nor_1_out);
  nor nor_3 (Q_4, and_3_out, Q_3);
  nor nor_4 (Q_3, Q_4, and_4_out);

  // Notes on the sheet:
  //   S: set
  //   R: reset
  //   rising edge toggling JK flip-flop without delay
  //   rising edge D flip-flop without delay
endmodule
